# Fritzing sketch DogProximityAlarmWTransistor (saved by Fritzing 0.9.10b)
circuit board: 8.46667cm x 5.64444cm
breadboards: 1

parts:
  Pico = Raspberry Pi Pico
  Diode = Rectifier Diode [part_number=1N4001 package="300 mil [THT]"]
  5V_Buzzer = Piezo Speaker
  Transistor = NPN-Transistor [package="TO92 [THT]"]
  Switch = Toggle Switch [package=THT]
  PIR = PIR sensor
  HK19F = DS2Y-5-DC5V [part_number=DS2Y-5-DC5V]
  On_/_Off = Tactile Switch Buttons - 12mm Square [package=tactile-pth-12mm]
  Diode_2 = Rectifier Diode [part_number=1N4001 package="300 mil [THT]"]

nets:
  N1: Pico.pin_3, Pico.pin_8, Pico.pin_13, Pico.pin_18, Pico.pin_23, Pico.pin_28, Pico.pin_33, Pico.pin_38, Pico.pin_42, Diode.anode, Switch.COM, PIR.GND, HK19F.16_-
  N2: Pico.pin_21, On_/_Off.1, On_/_Off.3, Diode_2.anode
  N3: Pico.pin_32, Transistor.B
  N4: Pico.pin_34, PIR.SIG, Diode_2.cathode
  N5: Pico.pin_36, Transistor.C, On_/_Off.2, On_/_Off.4
  N6: Pico.pin_40, HK19F.13_COM
  N7: Diode.cathode, Transistor.E, HK19F.1_+
  N8: 5V_Buzzer.pin1, Switch.L1
  N9: 5V_Buzzer.pin2, HK19F.9_N.O.

notes:
  DogProximityAlarm
  Gnd
  VDD 3V
  VDD 5V

custom parts:
  Raspberry Pi Pico: Raspberry Pi Pico. Based around the RP2040 microcontroller the Pico is a low cost microcontroller device bringing Raspberry Pi quality, cost, and easy of use to the microcontroller space. Jan 2021, Split part in to two versions: tht (this one) and SMD. This one will drill holes for a .1 in header in pcb to allow plugging in the module as well as providing pads to solder the module to the top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
  Tactile Switch Buttons - 12mm Square: Medium-sized clicky momentary switches are standard input "buttons" on electronic projects. These work best in a PCB but can be used on a solderless breadboard as shown in this tutorial. The pins are normally open (disconnected) and when the button is pressed they are momentarily closed. They come in a pack of 10, they're pretty handy so you'll want to keep them around. You can find an EAGLE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
